// Logisim project team40.circ as structural Verilog: 5 circuits, main circuit main
module main (
  output Done,
  output Reset,
  output Run,
  output [7:0] IR_DIN
);

  wire _0, _1, _2, _3, _4, _5, _6, _7, Ain, and_1_out, and_2_out, Asen, Bin, CLK, control_1_bout,
       control_1_clear, control_1_dinout, control_1_irin, control_1_mvi, or_1_out;
  wire [1:0] counter_2_q;
  wire [2:0] control_1_rx_yout;
  wire [3:0] counter_1_q;
  wire [7:0] A_q, alu_1_output, B_q, mux_1_output, R0, R1, R2, R3, R4, R5, R6, R7, register_1_q;

  Counter #(.width(4), .max('hf)) counter_1 (.Q(counter_1_q), .clk(or_1_out));  // open: load, D, count, carry, clr
  Clock clock_1 (.out(CLK));
  Hex_Digit_Display hex_digit_display_1 (.value(R0[3:0]));  // open: dp
  Hex_Digit_Display hex_digit_display_2 (.value(R0[7:4]));  // open: dp
  MUX mux_1 (
    .R0(R0), .R1(R1), .R2(R2), .R3(R3), .R4(R4), .R5(R5), .R6(R6), .R7(R7), .DIN(IR_DIN), .B(B_q),
    .RXout_Ryout(control_1_rx_yout), .DINout(control_1_dinout), .Bout(control_1_bout), .Output(mux_1_output));
  Register_part register_1 (.D(IR_DIN), .en(control_1_irin), .Q(register_1_q), .clk(CLK));  // open: clr
  ROM #(.addrWidth(4)) rom_1 (.addr(counter_1_q), .data(IR_DIN));  // open: sel
  Hex_Digit_Display hex_digit_display_3 (.value(R1[7:4]));  // open: dp
  Hex_Digit_Display hex_digit_display_4 (.value(R1[3:0]));  // open: dp
  Register register_2 (
    .R7_in(_7), .R6_in(_6), .R5_in(_5), .R4_in(_4), .R3_in(_3), .R2_in(_2), .R1_in(_1), .R0_in(_0),
    .Input(mux_1_output), .Clock(CLK), .R7_out(R7), .R6_out(R6), .R5_out(R5), .R4_out(R4), .R3_out(R3),
    .R2_out(R2), .R1_out(R1), .R0_out(R0));
  Counter #(.width(2), .max('h3)) counter_2 (
    .Q(counter_2_q), .clk(CLK), .clr(control_1_clear));  // open: load, D, count, carry
  Hex_Digit_Display hex_digit_display_5 (.value(R2[3:0]));  // open: dp
  Hex_Digit_Display hex_digit_display_6 (.value(R2[7:4]));  // open: dp
  Register_part A (.D(mux_1_output), .en(Ain), .Q(A_q), .clk(CLK));  // open: clr
  Hex_Digit_Display hex_digit_display_7 (.value(R3[7:4]));  // open: dp
  Hex_Digit_Display hex_digit_display_8 (.value(R3[3:0]));  // open: dp
  ALU alu_1 (.A_Rx(A_q), .Ry(mux_1_output), .Asen(Asen), .Output(alu_1_output));
  Control control_1 (
    .IR(register_1_q), .Bout(control_1_bout), .DINout(control_1_dinout), .Ain(Ain), .Asen(Asen), .Bin(Bin),
    .Clear(control_1_clear), .MSB(counter_2_q[1]), .LSB(counter_2_q[0]), .R0in(_0), .R1in(_1), .R2in(_2),
    .R3in(_3), .R4in(_4), .R5in(_5), .R6in(_6), .R7in(_7), .Run(Run), .IRin(control_1_irin), .Reset(Reset),
    .RX_Yout(control_1_rx_yout), .Done(Done), .mvi(control_1_mvi));
  Hex_Digit_Display hex_digit_display_9 (.value(R4[7:4]));  // open: dp
  Register_part B (.D(alu_1_output), .en(Bin), .Q(B_q), .clk(CLK));  // open: clr
  Hex_Digit_Display hex_digit_display_10 (.value(R5[7:4]));  // open: dp
  Hex_Digit_Display hex_digit_display_11 (.value(R4[3:0]));  // open: dp
  and and_1 (and_1_out, ~counter_2_q[1], counter_2_q[0]);  // AND_Gate
  Hex_Digit_Display hex_digit_display_12 (.value(R6[7:4]));  // open: dp
  Hex_Digit_Display hex_digit_display_13 (.value(R5[3:0]));  // open: dp
  and and_2 (and_2_out, and_1_out, control_1_mvi);
  Hex_Digit_Display hex_digit_display_14 (.value(R7[7:4]));  // open: dp
  Hex_Digit_Display hex_digit_display_15 (.value(R6[3:0]));  // open: dp
  or or_1 (or_1_out, Done, and_2_out);
  Hex_Digit_Display hex_digit_display_16 (.value(R7[3:0]));  // open: dp

  // Notes on the sheet:
  //   IR Register
  //   contents of rom_1 (hex, n*v repeats v):
  //   68 b8 35 68 6f b5 ad ee 40 1f 15 e8 ea 48 1 e9
endmodule

module Register (
  input  R0_in,
  input  R1_in,
  input  R2_in,
  input  R3_in,
  input  R4_in,
  input  R5_in,
  input  R6_in,
  input  R7_in,
  input  [7:0] Input,
  input  Clock,
  output [7:0] R7_out,
  output [7:0] R0_out,
  output [7:0] R1_out,
  output [7:0] R2_out,
  output [7:0] R3_out,
  output [7:0] R4_out,
  output [7:0] R5_out,
  output [7:0] R6_out
);

  Register_part R0 (.D(Input), .en(R0_in), .Q(R0_out), .clk(Clock));  // open: clr
  Register_part R1 (.D(Input), .en(R1_in), .Q(R1_out), .clk(Clock));  // open: clr
  Register_part R2 (.D(Input), .en(R2_in), .Q(R2_out), .clk(Clock));  // open: clr
  Register_part R3 (.D(Input), .en(R3_in), .Q(R3_out), .clk(Clock));  // open: clr
  Register_part R4 (.D(Input), .en(R4_in), .Q(R4_out), .clk(Clock));  // open: clr
  Register_part R5 (.D(Input), .en(R5_in), .Q(R5_out), .clk(Clock));  // open: clr
  Register_part R6 (.D(Input), .en(R6_in), .Q(R6_out), .clk(Clock));  // open: clr
  Register_part R7 (.D(Input), .en(R7_in), .Q(R7_out), .clk(Clock));  // open: clr
endmodule

module MUX (
  input  [7:0] R0,
  input  [7:0] R1,
  input  [7:0] R2,
  input  [7:0] R3,
  input  [2:0] RXout_Ryout,
  input  [7:0] DIN,
  input  [7:0] B,
  input  [7:0] R4,
  input  Bout,
  input  DINout,
  input  [7:0] R5,
  input  [7:0] R6,
  input  [7:0] R7,
  output [7:0] Output
);

  wire [7:0] multiplexer_1_out;

  Multiplexer #(.select(3), .width(8), .enable("false")) multiplexer_1 (
    .in0(R0), .in1(R1), .in2(R2), .in3(R3), .in4(R4), .in5(R5), .in6(R6), .in7(R7), .out(multiplexer_1_out),
    .sel(RXout_Ryout));
  Multiplexer #(.select(2), .width(8), .enable("false")) multiplexer_2 (
    .in0(multiplexer_1_out), .in1(DIN), .in2(B), .out(Output), .sel({Bout, DINout}));  // open: in3
endmodule

module ALU (
  input  [7:0] A_Rx,
  input  [7:0] Ry,
  input  Asen,
  output [7:0] Output
);

  wire [7:0] adder_1_out, subtractor_1_out;

  Adder adder_1 (.a(A_Rx), .b(Ry), .out(adder_1_out));  // open: cin, cout
  Subtractor subtractor_1 (.a(A_Rx), .b(Ry), .out(subtractor_1_out));  // open: bin, bout
  Multiplexer #(.width(8), .enable("false")) multiplexer_1 (
    .in0(adder_1_out), .in1(subtractor_1_out), .out(Output), .sel(Asen));
endmodule

module Control (
  input  MSB,
  input  LSB,
  input  [7:0] IR,
  output Ain,
  output Asen,
  output IRin,
  output Clear,
  output Run,
  output Bin,
  output Done,
  output R0in,
  output R1in,
  output DINout,
  output Bout,
  output R2in,
  output R3in,
  output R4in,
  output R5in,
  output R6in,
  output R7in,
  output [2:0] RX_Yout,
  output mvi,
  output Reset
);

  wire add, and_1_out, and_2_out, and_3_out, and_5_out, and_7_out, and_8_out, d_ff_1_q, d_ff_2_q, MV,
       or_1_out, or_2_out, or_3_out, or_4_out, or_5_out, or_6_out, or_7_out, or_8_out, or_9_out, sub,
       T10_4_out, T10_out, T11_2_out, T11_3_out;

  and T00 (IRin, ~MSB, ~LSB);  // AND_Gate
  and T11 (Bout, MSB, LSB);
  and T10 (T10_out, MSB, ~LSB);  // AND_Gate
  or or_1 (or_1_out, MV, DINout);
  or or_2 (or_2_out, sub, add);
  not not_1 (Run, IRin);
  Decoder #(.select(2), .enable("false")) decoder_1 (.out0(MV), .out1(DINout), .out2(add), .out3(sub), .sel(IR[7:6]));
  and T11_2 (T11_2_out, MSB, LSB);
  and and_1 (and_1_out, T10_out, or_1_out);
  and and_2 (and_2_out, T11_2_out, or_2_out);
  or or_3 (or_3_out, and_1_out, and_2_out);
  or or_4 (or_4_out, add, sub);
  and T01 (Ain, or_4_out, ~MSB, LSB);  // AND_Gate
  and and_3 (and_3_out, Bout, or_5_out);
  or or_5 (or_5_out, add, sub);
  D_Flip_Flop d_ff_1 (.clk(or_3_out), .D(1'b1), .Q(d_ff_1_q));  // open: Qn, preset, en, reset
  and T10_2 (Bin, or_4_out, MSB, ~LSB);  // AND_Gate
  or or_6 (or_6_out, MV, DINout, and_3_out);
  Multiplexer #(.select(2), .width(3), .enable("false")) multiplexer_1 (
    .in0(IR[2:0]), .in1(IR[5:3]), .in2(IR[2:0]), .out(RX_Yout), .sel({Bin, Ain}));  // open: in3
  and and_4 (Reset, d_ff_1_q, IRin);
  and and_5 (and_5_out, or_6_out, Run);
  Demultiplexer #(.select(3), .enable("false")) demultiplexer_1 (
    .out0(R0in), .out1(R1in), .out2(R2in), .out3(R3in), .out4(R4in), .out5(R5in), .out6(R6in), .out7(R7in),
    .in(and_5_out), .sel(IR[5:3]));
  and T10_3 (Asen, sub, MSB, ~LSB);  // AND_Gate
  and T10_4 (T10_4_out, MSB, ~LSB);  // AND_Gate
  or or_7 (or_7_out, MV, DINout);
  and and_6 (Clear, T10_4_out, or_7_out);
  and and_7 (and_7_out, T10_4_out, or_7_out);
  and and_8 (and_8_out, or_8_out, T11_3_out);
  or or_8 (or_8_out, sub, add);
  and T11_3 (T11_3_out, MSB, LSB);
  or or_9 (or_9_out, and_7_out, and_8_out);
  D_Flip_Flop d_ff_2 (.clk(or_9_out), .D(1'b1), .Q(d_ff_2_q));  // open: Qn, preset, en, reset
  and and_9 (Done, d_ff_2_q, IRin);

  assign mvi = DINout;

  // Other names for the same wires on the sheet: DC = IRin
endmodule
